// Logisim project lab11.circ as structural Verilog
module Ex1 (
  input  [7:0] In,
  output Out1,
  output [7:0] Out2
);

  and and_1 (Out1, In[0], In[7]);
  not not_1 (Out2[7], In[7]);

  assign Out2[6:0] = In[6:0];
endmodule

module rotr (
  input  [3:0] in_1,
  input  [15:0] in_2,
  output [15:0] out_3
);

  wire [1:0] multiplexer_1_out_2;
  wire [7:0] multiplexer_3_out, multiplexer_3_out_2;
  wire [13:0] multiplexer_1_out;
  wire [15:0] multiplexer_2_out;

  Multiplexer #(.width(16)) multiplexer_1 (
    .in0(in_2), .in1({in_2[0], in_2[15:1]}), .out({multiplexer_1_out, multiplexer_1_out_2}), .sel(in_1[0]));  // open: en
  Multiplexer #(.width(16)) multiplexer_2 (
    .in0({multiplexer_1_out, multiplexer_1_out_2}), .in1({multiplexer_1_out_2, multiplexer_1_out}),
    .out(multiplexer_2_out), .sel(in_1[1]));  // open: en
  Multiplexer #(.width(16)) multiplexer_3 (
    .in0(multiplexer_2_out), .in1({multiplexer_2_out[3:0], multiplexer_2_out[15:4]}),
    .out({multiplexer_3_out, multiplexer_3_out_2}), .sel(in_1[2]));  // open: en
  Multiplexer #(.width(16)) multiplexer_4 (
    .in0({multiplexer_3_out, multiplexer_3_out_2}), .in1({multiplexer_3_out_2, multiplexer_3_out}),
    .out(out_3), .sel(in_1[3]));  // open: en
endmodule

module fib15 (
  input  [10:0] in_1,
  output out_2,
  output [10:0] out_3
);

  wire clock_1_out;
  wire [10:0] counter_1_q, fn_1_q, fn_2_q;

  Register #(.width(11)) fn_1 (.D(out_3), .en(out_2), .Q(fn_1_q), .clk(clock_1_out));  // open: clr
  Clock clock_1 (.out(clock_1_out));
  Register #(.width(11)) fn_2 (.D(fn_1_q), .en(out_2), .Q(fn_2_q), .clk(clock_1_out));  // open: clr
  Counter #(.width(11), .max('h7ff), .ongoal("stay")) counter_1 (
    .Q(counter_1_q), .clk(clock_1_out));  // open: load, D, count, carry, clr
  Adder #(.width(11)) adder_1 (.a(fn_2_q), .b(fn_1_q), .out(out_3));  // open: cin, cout
  // Probe on counter_1_q
  Comparator #(.width(11), .mode("unsigned")) comparator_1 (.a(in_1), .b(counter_1_q), .gt(out_2));  // open: eq, lt
  // Probe on out_3
endmodule
